// Logisim project CIRCUITS.circ as structural Verilog: 13 circuits, main circuit HalfAdder
// HA
module HalfAdder (
  input  A,
  input  B,
  output Sum,
  output Carry_Out
);

  and and_1 (Carry_Out, A, B);
  xor xor_1 (Sum, A, B);
endmodule

// FA
module FullAdder (
  input  Carry_In,
  input  A,
  input  B,
  output Sum,
  output Carry_Out
);

  wire halfadder_1_carry_out, halfadder_1_sum, halfadder_2_carry_out;

  HalfAdder halfadder_1 (.A(A), .B(B), .Sum(halfadder_1_sum), .Carry_Out(halfadder_1_carry_out));
  HalfAdder halfadder_2 (.A(halfadder_1_sum), .B(Carry_In), .Sum(Sum), .Carry_Out(halfadder_2_carry_out));
  or or_1 (Carry_Out, halfadder_2_carry_out, halfadder_1_carry_out);
endmodule

module SRLatch (
  input  S,
  input  CLK,
  input  R,
  output Q,
  output Qn
);

  wire nand_1_out, nand_2_out;

  nand nand_1 (nand_1_out, S, CLK);
  nand nand_2 (nand_2_out, CLK, R);
  nand nand_3 (Q, nand_1_out, Qn);
  nand nand_4 (Qn, Q, nand_2_out);
endmodule

module Mem_4Bit (
  input  CLK,
  input  [3:0] Data_In,
  input  SET,
  input  RESET,
  input  Enable,
  output [3:0] Data_Out
);

  D_FF d_ff_1 (.Din(Data_In[0]), .CLK(CLK), .Dout(Data_Out[0]), .Enable(Enable), .SET(SET), .RESET(RESET));
  D_FF d_ff_2 (.Din(Data_In[1]), .CLK(CLK), .Dout(Data_Out[1]), .Enable(Enable), .SET(SET), .RESET(RESET));
  D_FF d_ff_3 (.Din(Data_In[2]), .CLK(CLK), .Dout(Data_Out[2]), .Enable(Enable), .SET(SET), .RESET(RESET));
  D_FF d_ff_4 (.Din(Data_In[3]), .CLK(CLK), .Dout(Data_Out[3]), .Enable(Enable), .SET(SET), .RESET(RESET));
endmodule

module Adder_4Bit (
  input  [3:0] B,
  input  [3:0] A,
  output [3:0] Result,
  output Overflow
);

  wire fulladder_2_carry_out, fulladder_3_carry_out, fulladder_4_carry_out;

  FullAdder fulladder_1 (.Carry_In(fulladder_2_carry_out), .A(A[3]), .B(B[3]), .Sum(Result[3]), .Carry_Out(Overflow));
  FullAdder fulladder_2 (
    .Carry_In(fulladder_3_carry_out), .A(A[2]), .B(B[2]), .Sum(Result[2]), .Carry_Out(fulladder_2_carry_out));
  FullAdder fulladder_3 (
    .Carry_In(fulladder_4_carry_out), .A(A[1]), .B(B[1]), .Sum(Result[1]), .Carry_Out(fulladder_3_carry_out));
  FullAdder fulladder_4 (.Carry_In(1'b0), .A(A[0]), .B(B[0]), .Sum(Result[0]), .Carry_Out(fulladder_4_carry_out));
endmodule

// D
module D_FF (
  input  SET,
  input  Din,
  input  CLK,
  input  Enable,
  input  RESET,
  output Dout
);

  wire and_1_out, and_2_out, nand_1_out, nand_2_out, nand_4_out, not_1_out, not_2_out, not_3_out, not_4_out,
       not_5_out, not_6_out;

  not not_1 (not_1_out, CLK);
  not not_2 (not_2_out, not_1_out);
  not not_3 (not_3_out, not_2_out);
  and and_1 (and_1_out, not_3_out, CLK);
  and and_2 (and_2_out, and_1_out, Enable);
  not not_4 (not_4_out, Din);
  nand nand_1 (nand_1_out, Din, and_2_out);
  nand nand_2 (nand_2_out, and_2_out, not_4_out);
  not not_5 (not_5_out, SET);
  not not_6 (not_6_out, RESET);
  nand nand_3 (Dout, nand_1_out, not_5_out, nand_4_out);
  nand nand_4 (nand_4_out, Dout, not_6_out, nand_2_out);
endmodule

// Grid_5X9
module Display (
  input  B,
  input  A,
  input  C,
  input  G,
  input  F,
  input  D,
  input  E,
  output [8:0] D4,
  output [8:0] D3,
  output [8:0] D2,
  output [8:0] D0,
  output [8:0] D1
);


  assign D0 = {1'b0, {3{D}}, 1'b0, {3{C}}, 1'b0};
  assign D1 = {B, 3'b000, G, 3'b000, E};
  assign D2 = {B, 3'b000, G, 3'b000, E};
  assign D3 = {B, 3'b000, G, 3'b000, E};
  assign D4 = {1'b0, {3{F}}, 1'b0, {3{A}}, 1'b0};
endmodule

module Display_5PANEL (
  input  ENABLE,
  input  RESET,
  input  SET,
  input  LOAD_SHIFT,
  input  [7:0] in_5,
  input  SERIAL_IN,
  input  ENABLE_CLK
);

  wire and_1_out, CLK_out, or_1_out;
  wire [7:0] mem_8bit_1_dout, mem_8bit_2_dout, mem_8bit_3_dout, mem_8bit_4_dout, mem_8bit_5_dout,
       multiplexer_1_out;
  wire [8:0] display_1_d0, display_1_d1, display_1_d2, display_1_d3, display_1_d4, display_2_d0,
       display_2_d1, display_2_d2, display_2_d3, display_2_d4, display_3_d0, display_3_d1, display_3_d2,
       display_3_d3, display_3_d4, display_4_d0, display_4_d1, display_4_d2, display_4_d3, display_4_d4,
       display_5_d0, display_5_d1, display_5_d2, display_5_d3, display_5_d4;

  DotMatrix #(.matrixrows(9)) dotmatrix_1 (
    .col0(display_1_d0), .col1(display_1_d1), .col2(display_1_d3), .col3(display_1_d2), .col4(display_1_d4));
  Display display_1 (
    .A(mem_8bit_1_dout[6]), .B(mem_8bit_1_dout[5]), .F(mem_8bit_1_dout[1]), .G(mem_8bit_1_dout[0]),
    .D(mem_8bit_1_dout[3]), .E(mem_8bit_1_dout[2]), .C(mem_8bit_1_dout[4]), .D4(display_1_d4),
    .D3(display_1_d3), .D1(display_1_d1), .D0(display_1_d0), .D2(display_1_d2));
  Mem_8Bit mem_8bit_1 (
    .Enable(ENABLE), .Din(multiplexer_1_out), .Dout(mem_8bit_1_dout), .CLK(or_1_out), .SET(RESET), .RESET(SET));
  Multiplexer #(.width(8), .enable("false")) multiplexer_1 (
    .in0(in_5), .in1(mem_8bit_5_dout), .out(multiplexer_1_out), .sel(LOAD_SHIFT));
  DotMatrix #(.matrixrows(9)) dotmatrix_2 (
    .col0(display_2_d0), .col1(display_2_d1), .col2(display_2_d3), .col3(display_2_d2), .col4(display_2_d4));
  Display display_2 (
    .A(mem_8bit_2_dout[6]), .B(mem_8bit_2_dout[5]), .F(mem_8bit_2_dout[1]), .G(mem_8bit_2_dout[0]),
    .D(mem_8bit_2_dout[3]), .E(mem_8bit_2_dout[2]), .C(mem_8bit_2_dout[4]), .D4(display_2_d4),
    .D3(display_2_d3), .D1(display_2_d1), .D0(display_2_d0), .D2(display_2_d2));
  Mem_8Bit mem_8bit_2 (
    .Enable(ENABLE), .Din(mem_8bit_1_dout), .Dout(mem_8bit_2_dout), .CLK(or_1_out), .SET(RESET), .RESET(SET));
  DotMatrix #(.matrixrows(9)) dotmatrix_3 (
    .col0(display_3_d0), .col1(display_3_d1), .col2(display_3_d3), .col3(display_3_d2), .col4(display_3_d4));
  DotMatrix #(.matrixrows(9)) dotmatrix_4 (
    .col0(display_4_d0), .col1(display_4_d1), .col2(display_4_d3), .col3(display_4_d2), .col4(display_4_d4));
  Display display_3 (
    .A(mem_8bit_3_dout[6]), .B(mem_8bit_3_dout[5]), .F(mem_8bit_3_dout[1]), .G(mem_8bit_3_dout[0]),
    .D(mem_8bit_3_dout[3]), .E(mem_8bit_3_dout[2]), .C(mem_8bit_3_dout[4]), .D4(display_3_d4),
    .D3(display_3_d3), .D1(display_3_d1), .D0(display_3_d0), .D2(display_3_d2));
  Mem_8Bit mem_8bit_3 (
    .Enable(ENABLE), .Din(mem_8bit_2_dout), .Dout(mem_8bit_3_dout), .CLK(or_1_out), .SET(RESET), .RESET(SET));
  Display display_4 (
    .A(mem_8bit_4_dout[6]), .B(mem_8bit_4_dout[5]), .F(mem_8bit_4_dout[1]), .G(mem_8bit_4_dout[0]),
    .D(mem_8bit_4_dout[3]), .E(mem_8bit_4_dout[2]), .C(mem_8bit_4_dout[4]), .D4(display_4_d4),
    .D3(display_4_d3), .D1(display_4_d1), .D0(display_4_d0), .D2(display_4_d2));
  Mem_8Bit mem_8bit_4 (
    .Enable(ENABLE), .Din(mem_8bit_3_dout), .Dout(mem_8bit_4_dout), .CLK(or_1_out), .SET(RESET), .RESET(SET));
  DotMatrix #(.matrixrows(9)) dotmatrix_5 (
    .col0(display_5_d0), .col1(display_5_d1), .col2(display_5_d3), .col3(display_5_d2), .col4(display_5_d4));
  Display display_5 (
    .A(mem_8bit_5_dout[6]), .B(mem_8bit_5_dout[5]), .F(mem_8bit_5_dout[1]), .G(mem_8bit_5_dout[0]),
    .D(mem_8bit_5_dout[3]), .E(mem_8bit_5_dout[2]), .C(mem_8bit_5_dout[4]), .D4(display_5_d4),
    .D3(display_5_d3), .D1(display_5_d1), .D0(display_5_d0), .D2(display_5_d2));
  Mem_8Bit mem_8bit_5 (
    .Enable(ENABLE), .Din(mem_8bit_4_dout), .Dout(mem_8bit_5_dout), .CLK(or_1_out), .SET(RESET), .RESET(SET));
  or or_1 (or_1_out, and_1_out, SERIAL_IN);
  and and_1 (and_1_out, CLK_out, ENABLE_CLK);
  Clock CLK (.out(CLK_out));
endmodule

// Bit8
module Mem_8Bit (
  input  [7:0] Din,
  input  CLK,
  input  SET,
  input  RESET,
  input  Enable,
  output [7:0] Dout
);

  Mem_4Bit mem_4bit_1 (.CLK(CLK), .SET(RESET), .Enable(Enable), .Data_In(Din[3:0]), .RESET(SET), .Data_Out(Dout[3:0]));
  Mem_4Bit mem_4bit_2 (.CLK(CLK), .SET(RESET), .Enable(Enable), .Data_In(Din[7:4]), .RESET(SET), .Data_Out(Dout[7:4]));
endmodule

module Circular_Shift (
  input  [7:0] in_1,
  input  in_2,
  output [7:0] out_3,
  output [7:0] out_4,
  output [7:0] out_5,
  output [7:0] out_6
);

  wire mem_8bit_1_p4;

  // Mem_8Bit mem_8bit_1: pin names not known; wires that end beside it: out_3, in_1, in_2, mem_8bit_1_p4
  Clock clock_1 (.out(mem_8bit_1_p4));
  // Mem_8Bit mem_8bit_2: pin names not known; wires that end beside it: out_4, out_3, in_2, mem_8bit_1_p4
  // Mem_8Bit mem_8bit_3: pin names not known; wires that end beside it: out_5, out_4, in_2, mem_8bit_1_p4
  // Mem_8Bit mem_8bit_4: pin names not known; wires that end beside it: out_6, out_5, in_2, mem_8bit_1_p4
endmodule

module JK_FF (
  input  Set,
  input  J,
  input  CLK,
  input  K,
  input  Reset,
  output Q,
  output Qn
);

  wire and_1_out, and_2_out, and_3_out, nand_1_out, nand_2_out, not_1_out, not_2_out, not_3_out, or_1_out,
       or_2_out;

  and and_1 (and_1_out, Qn, J);
  and and_2 (and_2_out, K, Q);
  not not_1 (not_1_out, CLK);
  not not_2 (not_2_out, not_1_out);
  not not_3 (not_3_out, not_2_out);
  or or_1 (or_1_out, Set, and_1_out);
  and and_3 (and_3_out, not_3_out, CLK);
  or or_2 (or_2_out, and_2_out, Reset);
  nand nand_1 (nand_1_out, or_1_out, and_3_out);
  nand nand_2 (nand_2_out, and_3_out, or_2_out);
  nand nand_3 (Q, nand_1_out, Qn);
  nand nand_4 (Qn, Q, nand_2_out);
endmodule

module MUX_2X1 (
  input  D0,
  input  D1,
  input  S0,
  output Y
);

  wire and_1_out, and_2_out, not_1_out;

  not not_1 (not_1_out, S0);
  and and_1 (and_1_out, D0, not_1_out);
  or or_1 (Y, and_1_out, and_2_out);
  and and_2 (and_2_out, D1, S0);
endmodule

module D_From_JK_FF (
  input  Din,
  input  CLK,
  input  Clear,
  output Dout
);

  wire and_1_out, and_2_out, and_3_out, nand_1_out, nand_2_out, nand_4_out, not_1_out, not_2_out, not_3_out,
       not_4_out, or_1_out;

  not not_1 (not_1_out, Din);
  and and_1 (and_1_out, nand_4_out, Din);
  not not_2 (not_2_out, CLK);
  not not_3 (not_3_out, not_2_out);
  and and_2 (and_2_out, not_1_out, Dout);
  not not_4 (not_4_out, not_3_out);
  and and_3 (and_3_out, not_4_out, CLK);
  or or_1 (or_1_out, and_2_out, Clear);
  nand nand_1 (nand_1_out, and_1_out, and_3_out);
  nand nand_2 (nand_2_out, and_3_out, or_1_out);
  nand nand_3 (Dout, nand_1_out, nand_4_out);
  nand nand_4 (nand_4_out, Dout, nand_2_out);
endmodule
